// Logisim project cpu.circ as structural Verilog: 1 circuit, main circuit cpu
module cpu (
  input  clk,
  input  [31:0] INSTRUCTION,
  input  [31:0] READ_DATA,
  output [31:0] WRITE_ADDRESS,
  output [31:0] PROGRAM_COUNTER,
  output [31:0] ra,
  output [31:0] sp,
  output [31:0] t0,
  output [31:0] t1,
  output [31:0] t2,
  output [31:0] s0,
  output [31:0] s1,
  output [31:0] a0,
  output [31:0] tohost,
  output [3:0] WRITE_ENABLE,
  output [31:0] WRITE_DATA
);

  wire ASel, BrEq, BrLt, BrUn, BSel, CSRSel, CSRWEn, PCSel, RegWEn;
  wire [1:0] WBSel;
  wire [2:0] ImmSel;
  wire [3:0] ALUSel;
  wire [4:0] register_1_q_2, register_1_q_3;
  wire [11:0] CSR_address;
  wire [14:0] register_1_q;
  wire [31:0] adder_1_out, imm, multiplexer_1_out, multiplexer_2_out, multiplexer_3_out, multiplexer_4_out,
       multiplexer_5_out, PC_n_4, PC_stored, rs1, WBData;

  Adder #(.width(32)) adder_1 (.a(PROGRAM_COUNTER), .b(32'h4), .out(adder_1_out));  // open: cin, cout
  Multiplexer #(.enable("false"), .width(32)) multiplexer_1 (
    .in0(adder_1_out), .in1(WRITE_ADDRESS), .out(multiplexer_1_out), .sel(PCSel));
  Multiplexer #(.enable("false"), .width(32)) multiplexer_2 (
    .in0(INSTRUCTION), .in1(32'h13), .out(multiplexer_2_out), .sel(PCSel));
  Register #(.width(32)) PC (.D(multiplexer_1_out), .en(1'b1), .clk(clk), .Q(PROGRAM_COUNTER));  // open: clr
  Register #(.width(32)) register_1 (
    .D(multiplexer_2_out), .en(1'b1), .clk(clk),
    .Q({CSR_address, register_1_q_2, register_1_q[14:12], register_1_q_3, register_1_q[6:0]}));  // open: clr
  Register #(.width(32)) register_2 (.D(adder_1_out), .en(1'b1), .clk(clk), .Q(PC_n_4));  // open: clr
  Register #(.width(32)) register_3 (.D(PROGRAM_COUNTER), .en(1'b1), .clk(clk), .Q(PC_stored));  // open: clr
  control_logic control_logic_1 (
    .CSRWen(CSRWEn), .PCSel(PCSel), .RegWEn(RegWEn), .ImmSel(ImmSel), .BrUn(BrUn), .ASel(ASel), .BSel(BSel),
    .ALUSel(ALUSel), .MemRW(WRITE_ENABLE[3]), .WBSel(WBSel), .CSRSel(CSRSel),
    .inst({CSR_address, register_1_q_2, register_1_q[14:12], register_1_q_3, register_1_q[6:0]}),
    .BrEq(BrEq), .BrLt(BrLt));
  regfile regfile_1 (
    .rs1(register_1_q_2), .rs2(CSR_address[4:0]), .rd(register_1_q_3), .Write_Data(WBData), .RegWEn(RegWEn),
    .clk(clk), .ra(ra), .sp(sp), .t0(t0), .t1(t1), .t2(t2), .s0(s0), .s1(s1), .a0(a0), .Read_Data_1(rs1),
    .Read_Data_2(WRITE_DATA));
  imm_gen imm_gen_1 (
    .inst({CSR_address, register_1_q_2, register_1_q[14:12], register_1_q_3, register_1_q[6:0]}),
    .ImmSel(ImmSel), .imm(imm));
  Multiplexer #(.enable("false"), .width(32)) multiplexer_3 (
    .in0(PC_stored), .in1(rs1), .out(multiplexer_3_out), .sel(ASel));
  Multiplexer #(.enable("false"), .width(32)) multiplexer_4 (
    .in0(WRITE_DATA), .in1(imm), .out(multiplexer_4_out), .sel(BSel));
  alu alu_1 (.Result(WRITE_ADDRESS), .A(multiplexer_3_out), .B(multiplexer_4_out), .ALUSel(ALUSel));
  branch_comp branch_comp_1 (.rs1(rs1), .rs2(WRITE_DATA), .BrUn(BrUn), .BrEq(BrEq), .BrLt(BrLt));
  Multiplexer #(.enable("false"), .width(32)) multiplexer_5 (
    .in0(imm), .in1(rs1), .out(multiplexer_5_out), .sel(CSRSel));
  Multiplexer #(.enable("false"), .select(2), .width(32)) multiplexer_6 (
    .in0(PC_n_4), .in1(WRITE_ADDRESS), .in2(READ_DATA), .out(WBData), .sel(WBSel));  // open: in3
  csr csr_1 (.CSR_address(CSR_address), .CSR_din(multiplexer_5_out), .CSR_WE(CSRWEn), .clk(clk), .tohost(tohost));

  assign WRITE_ENABLE[2:0] = {3{WRITE_ENABLE[3]}};

  // Other names for the same wires on the sheet: ALURes[31:0] = WRITE_ADDRESS; rs2[31:0] = WRITE_DATA;
  //   MemRW = WRITE_ENABLE[3]

  // Notes on the sheet:
  //   Output to IMEM
  //   IMEM (do **NOT** move this)
  //   beq t1, t2, good
  //   addi t1, t1, 22
  //   good: addi t1, t1, 222
  //   Inputs from IMEM
  //   Inputs/Outputs for testing. Do **NOT** move these.
  //   Just a bunch of combinational logic
  //   PC
  //   rs1
  //   rs2
  //   imm
  //   Just a bunch of combinational logic
  //   Outputs To DMEM
  //   imm
  //   rs1
  //   DMEM (do **NOT** move this)
  //   Inputs From DMEM
endmodule
